// Logisim project CPU_MONOCICLOFINAL.circ as structural Verilog: 8 circuits, main circuit main
module main (
  input  Reset,
  output [31:0] out_2
);

  wire alu_1_zero, alu_control_1_jr, ALUSrc, and_2_out, and_3_out, brch, Brch_Bne, CLK, CLK_out,
       comparator_1_eq, control_1_regwrite, J, Jal, Lbu, MemRead, MemtoReg, MemWrite, or_1_out, or_2_out,
       RegDst;
  wire [1:0] ALUOP;
  wire [2:0] ALUO;
  wire [4:0] lbd_down_1_rs, lbd_down_1_rt, multiplexer_1_out, multiplexer_2_out, rd, sh;
  wire [5:0] funct, op;
  wire [15:0] imm;
  wire [25:0] address;
  wire [27:0] bit_extender_1_out, shifter_1_out;
  wire [31:0] adder_1_out, alu_1_result, banco_reg_1_read_data2, ex_16_32, Inst, memoria_datos_1_readdata,
       multiplexer_3_out, multiplexer_4_out, multiplexer_6_out, multiplexer_7_out, multiplexer_8_out, PC,
       PC_4, Read_D1, shifter_2_out;

  // Probe on Inst
  // Probe on PC_4
  // Probe on PC
  Comparator #(.width(32)) comparator_1 (.a(Inst), .b(32'h800000c), .eq(comparator_1_eq));  // open: gt, lt
  Clock u_CLK (.out(CLK_out));
  Fetch fetch_1 (.Input_PC(PC), .CLK(CLK), .CLR(Reset), .PC(out_2), .PC_4(PC_4), .Instruction(Inst));
  // Probe on Inst
  and and_1 (CLK, ~comparator_1_eq, CLK_out);  // AND_Gate
  LBD_DOWN lbd_down_1 (
    .Instruction(Inst), .funct(funct), .imm(imm), .shampt(sh), .rd(rd), .rt(lbd_down_1_rt),
    .address(address), .rs(lbd_down_1_rs), .op(op));
  CONTROL control_1 (
    .codOp(op), .RegDst(RegDst), .Branch(brch), .MemRead(MemRead), .MemtoReg(MemtoReg), .MemWrite(MemWrite),
    .Jump(J), .Branch_Bne(Brch_Bne), .Jal(Jal), .Lbu(Lbu), .AluSrc(ALUSrc), .ALUOP(ALUOP),
    .RegWrite(control_1_regwrite));
  // Probe on address
  // Probe on rd
  // Probe on lbd_down_1_rs
  // Probe on lbd_down_1_rs
  Multiplexer #(.width(5)) multiplexer_1 (.in0(lbd_down_1_rt), .in1(rd), .out(multiplexer_1_out), .sel(RegDst));
  Multiplexer #(.width(5)) multiplexer_2 (.in0(multiplexer_1_out), .in1({5{1'b1}}), .out(multiplexer_2_out), .sel(Jal));
  // Probe on multiplexer_2_out
  // Probe on address
  assign bit_extender_1_out = {{2{address[25]}}, address};  // Bit_Extender bit_extender_1
  // Probe on PC_4
  // Probe on bit_extender_1_out
  Shifter #(.width(28)) shifter_1 (.in(bit_extender_1_out), .\dist (5'b00010), .out(shifter_1_out));
  // Probe on funct
  assign ex_16_32 = {{16{imm[15]}}, imm};  // Bit_Extender bit_extender_2
  // Probe on {PC_4[31:28], shifter_1_out}
  // Probe on ALUOP
  // Probe on Read_D1
  BANCO_REG banco_reg_1 (
    .RegWrite(control_1_regwrite), .write_reg(multiplexer_2_out), .Read_Reg1(lbd_down_1_rs),
    .Read_Reg2(lbd_down_1_rt), .Reset(Reset), .CLK(CLK), .Write_data(multiplexer_7_out),
    .Read_Data1(Read_D1), .Read_Data2(banco_reg_1_read_data2));
  Multiplexer #(.width(32)) multiplexer_3 (
    .in0(multiplexer_6_out), .in1({PC_4[31:28], shifter_1_out}), .out(multiplexer_3_out), .sel(or_1_out));
  or or_1 (or_1_out, Jal, J);
  Shifter #(.width(32)) shifter_2 (.in(ex_16_32), .\dist (5'b00010), .out(shifter_2_out));
  ALU_CONTROL alu_control_1 (.ALUOP(ALUOP), .FUNCT(funct), .JR(alu_control_1_jr), .ALUO(ALUO));
  Multiplexer #(.width(32)) multiplexer_4 (
    .in0(banco_reg_1_read_data2), .in1(ex_16_32), .out(multiplexer_4_out), .sel(ALUSrc));
  // Probe on banco_reg_1_read_data2
  // Probe on multiplexer_7_out
  Adder #(.width(32)) adder_1 (.a(PC_4), .b(shifter_2_out), .out(adder_1_out));  // open: cin, cout
  // Probe on ALUO
  Multiplexer #(.width(32)) multiplexer_5 (.in0(multiplexer_3_out), .in1(Read_D1), .out(PC), .sel(alu_control_1_jr));
  Multiplexer #(.width(32)) multiplexer_6 (.in0(PC_4), .in1(adder_1_out), .out(multiplexer_6_out), .sel(or_2_out));
  ALU alu_1 (
    .ALU_OPER(ALUO), .Operando_A(Read_D1), .Operando_B(multiplexer_4_out), .Result(alu_1_result),
    .zERO(alu_1_zero));
  // Probe on banco_reg_1_read_data2
  and and_2 (and_2_out, brch, alu_1_zero);
  and and_3 (and_3_out, ~alu_1_zero, Brch_Bne);  // AND_Gate
  or or_2 (or_2_out, and_2_out, and_3_out);
  Memoria_Datos memoria_datos_1 (
    .Address(alu_1_result), .MemWrite(MemWrite), .MemRead(MemRead), .CLK(CLK),
    .Write_Data(banco_reg_1_read_data2), .lbu(Lbu), .ReadData(memoria_datos_1_readdata));
  Multiplexer #(.width(32)) multiplexer_7 (.in0(multiplexer_8_out), .in1(PC_4), .out(multiplexer_7_out), .sel(Jal));
  // Probe on alu_1_result
  Multiplexer #(.width(32)) multiplexer_8 (
    .in0(alu_1_result), .in1(memoria_datos_1_readdata), .out(multiplexer_8_out), .sel(MemtoReg));
  // Probe on memoria_datos_1_readdata
  // Probe on multiplexer_8_out
endmodule

module Fetch (
  input  [31:0] Input_PC,
  input  CLK,
  input  CLR,
  output [31:0] PC,
  output [31:0] PC_4,
  output [31:0] Instruction
);

  Register #(.width(32)) register_1 (.D(Input_PC), .en(1'b1), .clk(CLK), .Q(PC), .clr(CLR));
  // Probe on PC
  Adder #(.width(32)) adder_1 (.a(PC), .b(32'h4), .out(PC_4));  // open: cin, cout
  // Probe on PC[25:2]
  ROM #(.addrWidth(24), .dataWidth(32)) rom_1 (.addr(PC[25:2]), .data(Instruction));
  // Probe on PC_4
  // Probe on Instruction

  // Notes on the sheet:
  //   contents of rom_1 (hex, n*v repeats v):
  //   8c10001c 8c050010 c00000c ac020000 c000036 404020 c000025 ac020008 2404020 c000025 ac02000c 800000b
  //   ac1f0082 8c0f0014 8c180018 2002020 f7020 4020 6020 4820 1125000c 8c8a0000 148582a 156e0005 982020
  //   12f4820 1406020 ac0c0004 8000014 1404020 982020 12f4820 8000014 1001020 1801820 8c1f0082 3e00008
  //   ac1f0082 8c0c0014 8c0d0018 2002020 5820 4820 8c080000 11250006 8c8a0000 150a0001 16c5820 12c4820
  //   8d2020 800002c 1601020 8c1f0082 3e00008 ac1f0082 8c0f0014 8c180018 2002020 f7020 4020 6020 4820
  //   8c880000 ac080004 1125000b 8c8a0000 148582a 156e0005 982020 12f4820 1404020 ac090004 8000040 982020
  //   12f4820 8000040 8c1f0082 3e00008
endmodule

module LBD_DOWN (
  input  [31:0] Instruction,
  output [5:0] funct,
  output [15:0] imm,
  output [4:0] shampt,
  output [4:0] rd,
  output [4:0] rt,
  output [25:0] address,
  output [4:0] rs,
  output [5:0] op
);


  assign address = Instruction[25:0];
  assign funct = Instruction[5:0];
  assign imm = Instruction[15:0];
  assign op = Instruction[31:26];
  assign rd = Instruction[15:11];
  assign rs = Instruction[25:21];
  assign rt = Instruction[20:16];
  assign shampt = Instruction[10:6];
endmodule

module BANCO_REG (
  input  RegWrite,
  input  [4:0] write_reg,
  input  [4:0] Read_Reg1,
  input  [4:0] Read_Reg2,
  input  Reset,
  input  CLK,
  input  [31:0] Write_data,
  output [31:0] Read_Data1,
  output [31:0] Read_Data2
);

  wire W0, W1, W2, W3, W4, W5, W6, W7, W8, W9, W10, W11, W12, W13, W14, W15, W16, W17, W18, W19, W20, W21,
       W22, W23, W24, W25, W26, W27, W28, W29, W30, W31;
  wire [31:0] a0, a1, a2, a3, at, fp, gp, k0, k1, ra, s0, s1, s2, s3, s4, s5, s6, s7, sp, t0, t1, t2, t3, t4,
       t5, t6, t7, t8, t9, v0, v1, z0;

  Decoder #(.select(5)) decoder_1 (
    .out0(W0), .out1(W1), .out2(W2), .out3(W3), .out4(W4), .out5(W5), .out6(W6), .out7(W7), .out8(W8),
    .out9(W9), .out10(W10), .out11(W11), .out12(W12), .out13(W13), .out14(W14), .out15(W15), .out16(W16),
    .out17(W17), .out18(W18), .out19(W19), .out20(W20), .out21(W21), .out22(W22), .out23(W23), .out24(W24),
    .out25(W25), .out26(W26), .out27(W27), .out28(W28), .out29(W29), .out30(W30), .out31(W31),
    .sel(write_reg), .en(RegWrite));
  Register #(.width(32)) u_t0 (.D(Write_data), .en(W8), .clk(CLK), .Q(t0), .clr(Reset));
  Register #(.width(32)) u_t1 (.D(Write_data), .en(W9), .clk(CLK), .Q(t1), .clr(Reset));
  Register #(.width(32)) u_t2 (.D(Write_data), .en(W10), .clk(CLK), .Q(t2), .clr(Reset));
  Register #(.width(32)) u_t3 (.D(Write_data), .en(W11), .clk(CLK), .Q(t3), .clr(Reset));
  Register #(.width(32)) u_t4 (.D(Write_data), .en(W12), .clk(CLK), .Q(t4), .clr(Reset));
  Register #(.width(32)) u_t5 (.D(Write_data), .en(W13), .clk(CLK), .Q(t5), .clr(Reset));
  Register #(.width(32)) u_t6 (.D(Write_data), .en(W14), .clk(CLK), .Q(t6), .clr(Reset));
  Register #(.width(32)) u_t7 (.D(Write_data), .en(W15), .clk(CLK), .Q(t7), .clr(Reset));
  Register #(.width(32)) u_t8 (.D(Write_data), .en(W24), .clk(CLK), .Q(t8), .clr(Reset));
  Register #(.width(32)) u_t9 (.D(Write_data), .en(W25), .clk(CLK), .Q(t9), .clr(Reset));
  Register #(.width(32)) u_s7 (.D(Write_data), .en(W23), .clk(CLK), .Q(s7), .clr(Reset));
  Register #(.width(32)) u_z0 (.D({32{1'b0}}), .en(W0), .clk(CLK), .Q(z0), .clr(Reset));
  Register #(.width(32)) u_at (.D(Write_data), .en(W1), .clk(CLK), .Q(at), .clr(Reset));
  Register #(.width(32)) u_s0 (.D(Write_data), .en(W16), .clk(CLK), .Q(s0), .clr(Reset));
  Register #(.width(32)) u_s1 (.D(Write_data), .en(W17), .clk(CLK), .Q(s1), .clr(Reset));
  Register #(.width(32)) u_s2 (.D(Write_data), .en(W18), .clk(CLK), .Q(s2), .clr(Reset));
  Register #(.width(32)) u_s3 (.D(Write_data), .en(W19), .clk(CLK), .Q(s3), .clr(Reset));
  Register #(.width(32)) u_s4 (.D(Write_data), .en(W20), .clk(CLK), .Q(s4), .clr(Reset));
  Register #(.width(32)) u_s5 (.D(Write_data), .en(W21), .clk(CLK), .Q(s5), .clr(Reset));
  Register #(.width(32)) u_s6 (.D(Write_data), .en(W22), .clk(CLK), .Q(s6), .clr(Reset));
  Register #(.width(32)) u_v0 (.D(Write_data), .en(W2), .clk(CLK), .Q(v0), .clr(Reset));
  Register #(.width(32)) u_v1 (.D(Write_data), .en(W3), .clk(CLK), .Q(v1), .clr(Reset));
  Register #(.width(32)) u_a0 (.D(Write_data), .en(W4), .clk(CLK), .Q(a0), .clr(Reset));
  Register #(.width(32)) u_a1 (.D(Write_data), .en(W5), .clk(CLK), .Q(a1), .clr(Reset));
  Register #(.width(32)) u_a2 (.D(Write_data), .en(W6), .clk(CLK), .Q(a2), .clr(Reset));
  Register #(.width(32)) u_a3 (.D(Write_data), .en(W7), .clk(CLK), .Q(a3), .clr(Reset));
  Register #(.width(32)) u_k0 (.D(Write_data), .en(W26), .clk(CLK), .Q(k0), .clr(Reset));
  Register #(.width(32)) u_k1 (.D(Write_data), .en(W27), .clk(CLK), .Q(k1), .clr(Reset));
  Register #(.width(32)) u_gp (.D(Write_data), .en(W28), .clk(CLK), .Q(gp), .clr(Reset));
  Register #(.width(32)) u_sp (.D(Write_data), .en(W29), .clk(CLK), .Q(sp), .clr(Reset));
  Register #(.width(32)) u_fp (.D(Write_data), .en(W30), .clk(CLK), .Q(fp), .clr(Reset));
  Register #(.width(32)) u_ra (.D(Write_data), .en(W31), .clk(CLK), .Q(ra), .clr(Reset));
  Multiplexer #(.select(5), .width(32)) multiplexer_1 (
    .in0(z0), .in1(at), .in2(v0), .in3(v1), .in4(a0), .in5(a1), .in6(a2), .in7(a3), .in8(t0), .in9(t1),
    .in10(t2), .in11(t3), .in12(t4), .in13(t5), .in14(t6), .in15(t7), .in16(s0), .in17(s1), .in18(s2),
    .in19(s3), .in20(s4), .in21(s5), .in22(s6), .in23(s7), .in24(t8), .in25(t9), .in26(k0), .in27(k1),
    .in28(gp), .in29(sp), .in30(fp), .in31(ra), .out(Read_Data1), .sel(Read_Reg1));
  Multiplexer #(.select(5), .width(32)) multiplexer_2 (
    .in0(z0), .in1(at), .in2(v0), .in3(v1), .in4(a0), .in5(a1), .in6(a2), .in7(a3), .in8(t0), .in9(t1),
    .in10(t2), .in11(t3), .in12(t4), .in13(t5), .in14(t6), .in15(t7), .in16(s0), .in17(s1), .in18(s2),
    .in19(s3), .in20(s4), .in21(s5), .in22(s6), .in23(s7), .in24(t8), .in25(t9), .in26(k0), .in27(k1),
    .in28(gp), .in29(sp), .in30(fp), .in31(ra), .out(Read_Data2), .sel(Read_Reg2));
endmodule

module ALU (
  input  [2:0] ALU_OPER,
  input  [31:0] Operando_A,
  input  [31:0] Operando_B,
  output [31:0] Result,
  output zERO
);

  wire CMP;
  wire [31:0] ADD, AND1, NOR1, ORD1, SUB;
  wire [31:1] SLT;

  Adder #(.width(32)) adder_1 (.a(Operando_A), .b(Operando_B), .out(ADD));  // open: cin, cout
  Subtractor #(.width(32)) subtractor_1 (.a(Operando_A), .b(Operando_B), .out(SUB));  // open: bin, bout
  Comparator #(.width(32)) comparator_1 (.a(Operando_A), .b(Operando_B), .lt(CMP));  // open: gt, eq
  assign AND1 = Operando_A & Operando_B;  // AND_Gate and_1, 32 bits wide
  assign ORD1 = Operando_A | Operando_B;  // OR_Gate or_1, 32 bits wide
  assign NOR1 = ~(Operando_A | Operando_B);  // NOR_Gate nor_1, 32 bits wide
  // Probe on ADD
  // Probe on SUB
  // Probe on CMP
  Multiplexer #(.select(3), .width(32)) multiplexer_1 (
    .in0(ADD), .in1(SUB), .in2(AND1), .in3(ORD1), .in4(NOR1), .in5({SLT, CMP}), .out(Result), .sel(ALU_OPER));  // open: in6, in7
  Comparator #(.width(32)) comparator_2 (.a(Result), .b({32{1'b0}}), .eq(zERO));  // open: gt, lt

  // Other names for the same wires on the sheet: A[31:0] = Operando_A; B[31:0] = Operando_B; SLT[0] = CMP
endmodule

module CONTROL (
  input  [5:0] codOp,
  output RegDst,
  output Branch,
  output MemRead,
  output MemtoReg,
  output MemWrite,
  output Jump,
  output Branch_Bne,
  output Jal,
  output Lbu,
  output AluSrc,
  output [1:0] ALUOP,
  output RegWrite
);

  wire multiplexer_1_out, multiplexer_2_out, multiplexer_3_out, multiplexer_4_out, or_3_out;

  and and_1 (Branch_Bne, codOp[0], ~codOp[1], codOp[2], ~codOp[3], ~codOp[4], ~codOp[5]);  // AND_Gate
  and and_2 (RegDst, ~codOp[0], ~codOp[1], ~codOp[2], ~codOp[3], ~codOp[4], ~codOp[5]);  // AND_Gate
  or or_1 (AluSrc, MemWrite, Lbu, MemRead);
  and and_3 (MemRead, codOp[0], codOp[1], ~codOp[2], ~codOp[3], ~codOp[4], codOp[5]);  // AND_Gate
  or or_2 (RegWrite, RegDst, MemRead, Lbu, Jal);
  and and_4 (MemWrite, codOp[0], codOp[1], ~codOp[2], codOp[3], ~codOp[4], codOp[5]);  // AND_Gate
  and and_5 (Branch, ~codOp[0], ~codOp[1], codOp[2], ~codOp[3], ~codOp[4], ~codOp[5]);  // AND_Gate
  and and_6 (Jump, ~codOp[0], codOp[1], ~codOp[2], ~codOp[3], ~codOp[4], ~codOp[5]);  // AND_Gate
  and and_7 (Jal, codOp[0], codOp[1], ~codOp[2], ~codOp[3], ~codOp[4], ~codOp[5]);  // AND_Gate
  or or_3 (or_3_out, MemRead, MemWrite, Lbu);
  and and_8 (Lbu, ~codOp[0], ~codOp[1], codOp[2], ~codOp[3], ~codOp[4], codOp[5]);  // AND_Gate
  Multiplexer multiplexer_1 (.in0(1'b0), .in1(1'b1), .out(multiplexer_1_out), .sel(Branch));
  Multiplexer multiplexer_2 (.in0(1'b0), .in1(1'b1), .out(multiplexer_2_out), .sel(Branch_Bne));
  Multiplexer multiplexer_3 (.in0(1'b0), .in1(1'b1), .out(multiplexer_3_out), .sel(RegDst));
  Multiplexer multiplexer_4 (.in0(1'b0), .in1(1'b0), .out(multiplexer_4_out), .sel(or_3_out));
  or or_4 (ALUOP[0], multiplexer_1_out, multiplexer_2_out);
  or or_5 (ALUOP[1], multiplexer_3_out, multiplexer_4_out);

  assign MemtoReg = MemRead;

  // Other names for the same wires on the sheet: beq = Branch; bne = Branch_Bne; j = Jump; lw = MemRead;
  //   R_Format = RegDst; sw = MemWrite
endmodule

module ALU_CONTROL (
  input  [1:0] ALUOP,
  input  [5:0] FUNCT,
  output JR,
  output [2:0] ALUO
);

  wire and_2_out;
  wire [2:0] rom_1_data, rom_2_data;

  ROM #(.addrWidth(2), .dataWidth(3)) rom_1 (.addr(ALUOP), .data(rom_1_data));
  ROM #(.addrWidth(6), .dataWidth(3)) rom_2 (.addr(FUNCT), .data(rom_2_data));
  and and_1 (JR, ~FUNCT[0], ~FUNCT[1], ~FUNCT[2], FUNCT[3], ~FUNCT[4], ~FUNCT[5]);  // AND_Gate
  // Probe on rom_2_data
  // Probe on ALUO
  Multiplexer #(.width(3)) multiplexer_1 (.in0(rom_1_data), .in1(rom_2_data), .out(ALUO), .sel(and_2_out));
  and and_2 (and_2_out, ~ALUOP[0], ALUOP[1]);  // AND_Gate

  // Notes on the sheet:
  //   contents of rom_1 (hex, n*v repeats v):
  //   0 1 2
  //   contents of rom_2 (hex, n*v repeats v):
  //   34*0 1 0 2 3 0 4 0 0 5
endmodule

module Memoria_Datos (
  input  [31:0] Address,
  input  MemWrite,
  input  MemRead,
  input  CLK,
  input  [31:0] Write_Data,
  input  lbu,
  output [31:0] ReadData
);

  wire [7:0] multiplexer_2_out;
  wire [31:0] bit_extender_1_out, ram_1_dout;

  RAM #(.addrWidth(24), .asyncread("true"), .dataWidth(32)) ram_1 (
    .addr(Address[25:2]), .we(MemWrite), .oe(MemRead), .clk(CLK), .din(Write_Data), .dout(ram_1_dout));
  Multiplexer #(.width(32)) multiplexer_1 (.in0(ram_1_dout), .in1(bit_extender_1_out), .out(ReadData), .sel(lbu));
  Multiplexer #(.select(2), .width(8)) multiplexer_2 (
    .in0(ram_1_dout[7:0]), .in1(ram_1_dout[15:8]), .in2(ram_1_dout[23:16]), .in3(ram_1_dout[31:24]),
    .out(multiplexer_2_out), .sel(Address[1:0]));
  assign bit_extender_1_out = {{24{1'b0}}, multiplexer_2_out};  // Bit_Extender bit_extender_1
  // Probe on bit_extender_1_out

  // Other names for the same wires on the sheet: S2[1:0] = Address[1:0]
endmodule
